// Logisim project part2.circ as structural Verilog
module AddMachine (
  output [7:0] out_1,
  output [7:0] out_2
);

  wire clock_1_out;

  Adder adder_1 (.a(8'h1), .b(out_2), .out(out_1));  // open: cin, cout
  Register register_1 (.D(out_1), .clk(clock_1_out), .Q(out_2));  // open: en, clr
  Clock clock_1 (.out(clock_1_out));

  // Notes on the sheet:
  //   ADD_OUT
  //   REG_OUT
endmodule
