// Logisim project alu.circ as structural Verilog: 1 circuit, main circuit alu
module alu (
  input  [31:0] A,
  input  [31:0] B,
  input  [3:0] ALUSel,
  output [31:0] Result
);

  wire comparator_3_eq, comparator_4_eq;
  wire [0:0] sir_res, slt_res, sltu_res;
  wire [6:0] cnto_res;
  wire [31:0] add_res, adder_2_out, and_res, bit_extender_1_out, bit_extender_2_out, bit_extender_3_out,
       bit_extender_4_out, bitpal_res, div_res, mul_res, mulh_res, mulhu_res, multiplier_3_out,
       multiplier_4_out, or_res, rem_res, sll_res, sra_res, srl_res, sub_res, xor_res;

  Multiplexer #(.select(4), .width(32), .enable("false")) multiplexer_1 (
    .in0(add_res), .in1(sub_res), .in2(mulh_res), .in3(mul_res), .in4(div_res), .in5(rem_res), .in6(and_res),
    .in7(or_res), .in8(xor_res), .in9(sll_res), .in10({{31{1'b0}}, slt_res[0]}), .in11(sra_res),
    .in12(srl_res), .in13(mulhu_res), .in14({{31{1'b0}}, sltu_res[0]}), .in15({{31{1'b0}}, sir_res[0]}),
    .out(Result), .sel(ALUSel));
  Adder #(.width(32)) adder_1 (.a(A), .b(B), .out(add_res));  // open: cin, cout
  Subtractor #(.width(32)) subtractor_1 (.a(A), .b(B), .out(sub_res));  // open: bin, bout
  Multiplier #(.width(32)) multiplier_1 (.a(A), .b(B), .cout(mulhu_res));  // open: out, cin
  Multiplier #(.width(32)) multiplier_2 (.a(A), .b(B), .out(mul_res));  // open: cin, cout
  Divider #(.width(32)) divider_1 (.a(A), .b(B), .out(div_res));  // open: upper, rem
  Divider #(.width(32)) divider_2 (.a(A), .b(B), .rem(rem_res));  // open: out, upper
  assign and_res = A & B;  // AND_Gate and_1, 32 bits wide
  assign or_res = A | B;  // OR_Gate or_1, 32 bits wide
  assign xor_res = A ^ B;  // XOR_Gate xor_1, 32 bits wide
  Shifter #(.width(32)) shifter_1 (.in(A), .\dist (B[4:0]), .out(sll_res));
  Comparator #(.width(32)) comparator_1 (.a(A), .b(B), .lt(slt_res[0]));  // open: gt, eq
  Shifter #(.width(32), .shift("ar")) shifter_2 (.in(A), .\dist (B[4:0]), .out(sra_res));
  Shifter #(.width(32), .shift("lr")) shifter_3 (.in(A), .\dist (B[4:0]), .out(srl_res));
  BitAdder #(.width(32)) bitadder_1 (.in0(A), .in1(B), .out(cnto_res));
  Comparator #(.width(32), .mode("unsigned")) comparator_2 (.a(A), .b(B), .lt(sltu_res[0]));  // open: gt, eq
  Comparator #(.width(16)) comparator_3 (
    .a({A[0], A[1], A[2], A[3], A[4], A[5], A[6], A[7], A[8], A[9], A[10], A[11], A[12], A[13], A[14], A[15]}),
    .b(A[31:16]), .eq(comparator_3_eq));  // open: gt, lt
  Comparator #(.width(16)) comparator_4 (
    .a({B[0], B[1], B[2], B[3], B[4], B[5], B[6], B[7], B[8], B[9], B[10], B[11], B[12], B[13], B[14], B[15]}),
    .b(B[31:16]), .eq(comparator_4_eq));  // open: gt, lt
  Comparator #(.width(32)) comparator_5 (
    .a(A),
    .b({B[0], B[1], B[2], B[3], B[4], B[5], B[6], B[7], B[8], B[9], B[10], B[11], B[12], B[13], B[14], B[15], B[16], B[17], B[18], B[19], B[20], B[21], B[22], B[23], B[24], B[25], B[26], B[27], B[28], B[29], B[30], B[31]}),
    .eq(sir_res[0]));  // open: gt, lt
  assign bit_extender_1_out = {{31{1'b0}}, comparator_3_eq};  // Bit_Extender bit_extender_1
  assign bit_extender_2_out = {{31{1'b0}}, comparator_4_eq};  // Bit_Extender bit_extender_2
  assign bit_extender_3_out = {{31{A[31]}}, A[31]};  // Bit_Extender bit_extender_3
  assign bit_extender_4_out = {{31{B[31]}}, B[31]};  // Bit_Extender bit_extender_4
  assign bitpal_res = bit_extender_1_out | bit_extender_2_out;  // OR_Gate or_2, 32 bits wide
  Multiplier #(.width(32)) multiplier_3 (.a(bit_extender_3_out), .b(B), .out(multiplier_3_out));  // open: cin, cout
  Multiplier #(.width(32)) multiplier_4 (.a(A), .b(bit_extender_4_out), .out(multiplier_4_out));  // open: cin, cout
  Adder #(.width(32)) adder_2 (.a(multiplier_3_out), .b(multiplier_4_out), .out(adder_2_out));  // open: cin, cout
  Adder #(.width(32)) adder_3 (.a(adder_2_out), .b(mulhu_res), .out(mulh_res));  // open: cin, cout

  // Other names for the same wires on the sheet: B5[4:0] = B[4:0]

  // Notes on the sheet:
  //   INPUTS to your circuit
  //   DON'T CHANGE THE LOCATIONS OF THE INPUTS AND OUTPUTS!
  //   OUTPUT from your circuit
endmodule
