// Logisim project cpu.circ as structural Verilog: 5 circuits, main circuit main
module main (
  input  [31:0] INSTRUCTION,
  input  CLOCK,
  output [31:0] FETCH_ADDRESS,
  output [31:0] ra,
  output [31:0] sp,
  output [31:0] t0,
  output [31:0] t1,
  output [31:0] t2,
  output [31:0] s0,
  output [31:0] s1,
  output [31:0] a0
);

  wire BrEq, BrLT, BrUn, BSel, InstSel, MemRW, PCSel, RegWEn;
  wire [1:0] ASel, WBSel;
  wire [2:0] DataSel, ImmSel;
  wire [3:0] ALUSel;
  wire [31:0] adder_1_out, bit_extender_1_out, bit_extender_2_out, bit_extender_3_out, bit_extender_4_out,
       DMEM_datar, Inst, m_alu, m_DataA, m_DataB, m_imm, m_mem, m_pc, m_pc_plus_4, m_wb, multiplexer_1_out,
       multiplexer_2_out, multiplexer_3_out, multiplexer_4_out, PC_F_q;

  Adder #(.width(32)) adder_1 (.a(PC_F_q), .b(32'h4), .out(adder_1_out));  // open: cin, cout
  Multiplexer #(.width(32), .enable("false")) multiplexer_1 (
    .in0(adder_1_out), .in1(m_alu), .out(multiplexer_1_out), .sel(PCSel));
  Register #(.width(32)) PC_F (.D(multiplexer_1_out), .en(1'b1), .clk(CLOCK), .Q(PC_F_q));  // open: clr
  BranchComp branchcomp_1 (.DataA(m_DataA), .DataB(m_DataB), .BrUn(BrUn), .BrEq(BrEq), .BrLT(BrLT));
  Shifter #(.width(32), .shift("lr")) shifter_1 (.in(PC_F_q), .\dist (5'b00010), .out(FETCH_ADDRESS));
  Adder #(.width(32)) adder_2 (.a(m_pc), .b(32'h4), .out(m_pc_plus_4));  // open: cin, cout
  ImmGen ImmG (.ImmInput(Inst[31:7]), .ImmSel(ImmSel), .ImmOut(m_imm));
  Multiplexer #(.width(32), .enable("false")) multiplexer_2 (
    .in0(INSTRUCTION), .in1(32'h13), .out(multiplexer_2_out), .sel(InstSel));
  Register #(.width(32)) PC_D (.D(PC_F_q), .en(1'b1), .clk(CLOCK), .Q(m_pc));  // open: clr
  Register #(.width(32)) InstD (.D(multiplexer_2_out), .en(1'b1), .clk(CLOCK), .Q(Inst));  // open: clr
  Multiplexer #(.select(2), .width(32), .enable("false")) multiplexer_3 (
    .in0(m_DataA), .in1(m_pc), .in2({32{1'b0}}), .out(multiplexer_3_out), .sel(ASel));  // open: in3
  Multiplexer #(.width(32), .enable("false")) multiplexer_4 (
    .in0(m_DataB), .in1(m_imm), .out(multiplexer_4_out), .sel(BSel));
  mem_main DMEM (.Address(m_alu), .DataW(m_DataB), .MemRW(MemRW), .DataR(DMEM_datar), .clk(CLOCK));
  Multiplexer #(.select(2), .width(32), .enable("false")) multiplexer_5 (
    .in0(m_mem), .in1(m_alu), .in2(m_pc_plus_4), .out(m_wb), .sel(WBSel));  // open: in3
  assign bit_extender_1_out = {{24{DMEM_datar[7]}}, DMEM_datar[7:0]};  // Bit_Extender bit_extender_1
  assign bit_extender_2_out = {{16{DMEM_datar[15]}}, DMEM_datar[15:0]};  // Bit_Extender bit_extender_2
  assign bit_extender_3_out = {{24{1'b0}}, DMEM_datar[7:0]};  // Bit_Extender bit_extender_3
  assign bit_extender_4_out = {{16{1'b0}}, DMEM_datar[15:0]};  // Bit_Extender bit_extender_4
  alu Arithmetic_Logic_Unit (.A(multiplexer_3_out), .B(multiplexer_4_out), .ALUSel(ALUSel), .Result(m_alu));
  Multiplexer #(.select(3), .width(32), .enable("false")) multiplexer_6 (
    .in0(bit_extender_1_out), .in1(bit_extender_2_out), .in2(DMEM_datar), .in3(bit_extender_3_out),
    .in4(bit_extender_4_out), .out(m_mem), .sel(DataSel));  // open: in5, in6, in7
  regfile_main RegFile (
    .rs2(Inst[24:20]), .rd(Inst[11:7]), .Read_Data_1(m_DataA), .Read_Data_2(m_DataB), .ra(ra), .sp(sp),
    .t0(t0), .t1(t1), .t2(t2), .s0(s0), .s1(s1), .a0(a0), .rs1(Inst[19:15]), .Write_Data(m_wb),
    .RegWEn(RegWEn), .clk(CLOCK));
  Control controller (
    .Inst(Inst), .BrEq(BrEq), .BrLT(BrLT), .PCSel(PCSel), .InstSel(InstSel), .ImmSel(ImmSel),
    .RegWEn(RegWEn), .BrUn(BrUn), .ASel(ASel), .BSel(BSel), .ALUSel(ALUSel), .MemRW(MemRW),
    .DataSel(DataSel), .WBSel(WBSel));
  // Probe on WBSel
  // Probe on RegWEn
  // Probe on ALUSel
  // Probe on MemRW
  // Probe on BSel
  // Probe on ASel
  // Probe on BrUn
  // Probe on ImmSel
  // Probe on PCSel
  // Probe on DataSel

  // Other names for the same wires on the sheet: clk = CLOCK; fetch_addr[31:0] = FETCH_ADDRESS;
  //   m_AddrD[4:0] = Inst[11:7]; m_AddrA[4:0] = Inst[19:15]; m_AddrB[4:0] = Inst[24:20]

  // Notes on the sheet:
  //   Output
  //   Inputs/Outputs from run.circ. DO NOT MOVE THESE.
  //   Inputs
  //   IF
  //   ID
  //   EX
  //   MEM
  //   WB
  //   It is OK to move the PC, RegFile, ALU, and MEM to wherever is most convenient for you when constructing your CPU, and to delete this text
  //   Inputs/Outputs from run.circ. DO NOT MOVE THESE.
  //   Control TODO
endmodule

module ImmGen (
  input  [24:0] ImmInput,
  input  [2:0] ImmSel,
  output [31:0] ImmOut
);

  wire [31:0] bit_extender_1_out, bit_extender_2_out, bit_extender_3_out, bit_extender_4_out,
       bit_extender_5_out;

  assign bit_extender_1_out = {{20{ImmInput[24]}}, ImmInput[24:13]};  // Bit_Extender bit_extender_1
  assign bit_extender_2_out = {{20{ImmInput[24]}}, {ImmInput[24:18], ImmInput[4:0]}};  // Bit_Extender bit_extender_2
  assign bit_extender_3_out = {{19{ImmInput[24]}}, {ImmInput[24], ImmInput[0], ImmInput[23:18], ImmInput[4:1], 1'b0}};  // Bit_Extender bit_extender_3
  assign bit_extender_4_out = {{11{ImmInput[24]}}, {ImmInput[24], ImmInput[12:5], ImmInput[13], ImmInput[23:14], 1'b0}};  // Bit_Extender bit_extender_4
  assign bit_extender_5_out = {{27{1'b0}}, ImmInput[17:13]};  // Bit_Extender bit_extender_5
  Multiplexer #(.select(3), .width(32), .enable("false")) multiplexer_1 (
    .in0(bit_extender_1_out), .in1(bit_extender_2_out), .in2(bit_extender_3_out),
    .in3({ImmInput[24:5], {12{1'b0}}}), .in4(bit_extender_4_out), .in5(bit_extender_5_out), .out(ImmOut),
    .sel(ImmSel));  // open: in6, in7

  // Notes on the sheet:
  //   I
  //   S
  //   B
  //   U
  //   J
  //   L
endmodule

module BranchComp (
  input  [31:0] DataA,
  input  [31:0] DataB,
  input  BrUn,
  output BrEq,
  output BrLT
);

  wire comparator_1_eq, comparator_1_lt, comparator_2_eq, comparator_2_lt;

  Comparator #(.width(32)) comparator_1 (.a(DataA), .b(DataB), .eq(comparator_1_eq), .lt(comparator_1_lt));  // open: gt
  Comparator #(.width(32), .mode("unsigned")) comparator_2 (
    .a(DataA), .b(DataB), .eq(comparator_2_eq), .lt(comparator_2_lt));  // open: gt
  Multiplexer #(.enable("false")) multiplexer_1 (.in0(comparator_1_eq), .in1(comparator_2_eq), .out(BrEq), .sel(BrUn));
  Multiplexer #(.enable("false")) multiplexer_2 (.in0(comparator_1_lt), .in1(comparator_2_lt), .out(BrLT), .sel(BrUn));
endmodule

module Control (
  input  [31:0] Inst,
  input  BrEq,
  input  BrLT,
  output PCSel,
  output InstSel,
  output [2:0] ImmSel,
  output RegWEn,
  output BrUn,
  output [1:0] ASel,
  output BSel,
  output [3:0] ALUSel,
  output MemRW,
  output [2:0] DataSel,
  output [1:0] WBSel
);

  wire AIType, AluAdd, AluAnd, AluDivu, AluMulh, AluMulhu, AluMult, AluOr, AluRemu, AluSll, AluSlt, AluSltu,
       AluSra, AluSrl, AluSub, AluXor, and_2_out, and_10_out, and_11_out, and_12_out, and_13_out, and_14_out,
       and_33_out, AUType, BType, comparator_10_eq, comparator_11_eq, comparator_12_eq, comparator_13_eq,
       comparator_14_eq, comparator_15_eq, comparator_16_eq, comparator_17_eq, comparator_18_eq,
       comparator_19_eq, comparator_20_eq, comparator_21_eq, comparator_22_eq, comparator_23_eq,
       comparator_24_eq, comparator_25_eq, comparator_26_eq, comparator_27_eq, comparator_28_eq,
       comparator_29_eq, comparator_30_eq, comparator_31_eq, comparator_32_eq, comparator_33_eq,
       comparator_34_eq, comparator_35_eq, IType, JIType, JType, LIType, not_1_out, not_2_out, not_3_out,
       not_4_out, or_2_out, or_3_out, or_6_out, or_8_out, or_9_out, or_10_out, or_11_out, or_12_out,
       or_13_out, PCAluB, PCAluJ, RType, UType;
  wire [1:0] multiplexer_8_out, multiplexer_25_out;
  wire [2:0] multiplexer_7_out, multiplexer_14_out, multiplexer_16_out, multiplexer_20_out,
       multiplexer_23_out, multiplexer_27_out, multiplexer_28_out, multiplexer_29_out, multiplexer_30_out;
  wire [3:0] multiplexer_2_out, multiplexer_3_out, multiplexer_4_out, multiplexer_5_out, multiplexer_6_out,
       multiplexer_9_out, multiplexer_10_out, multiplexer_11_out, multiplexer_12_out, multiplexer_13_out,
       multiplexer_17_out, multiplexer_18_out, multiplexer_19_out, multiplexer_21_out;
  wire [6:0] multiplexer_1_out;

  Comparator #(.width(7)) comparator_1 (.a(Inst[6:0]), .b(7'b0110011), .eq(RType));  // open: gt, lt
  Comparator #(.width(7)) comparator_2 (.a(Inst[6:0]), .b(7'b0000011), .eq(LIType));  // open: gt, lt
  Comparator #(.width(7)) comparator_3 (.a(Inst[6:0]), .b(7'b0010011), .eq(AIType));  // open: gt, lt
  Comparator #(.width(7)) comparator_4 (.a(Inst[6:0]), .b(7'b0100011), .eq(MemRW));  // open: gt, lt
  Comparator #(.width(7)) comparator_5 (.a(Inst[6:0]), .b(7'b1100011), .eq(BType));  // open: gt, lt
  Comparator #(.width(7)) comparator_6 (.a(Inst[6:0]), .b(7'b0010111), .eq(AUType));  // open: gt, lt
  Comparator #(.width(7)) comparator_7 (.a(Inst[6:0]), .b(7'b0110111), .eq(UType));  // open: gt, lt
  Comparator #(.width(7)) comparator_8 (.a(Inst[6:0]), .b(7'b1101111), .eq(JType));  // open: gt, lt
  Comparator #(.width(7)) comparator_9 (.a(Inst[6:0]), .b(7'b1100111), .eq(JIType));  // open: gt, lt
  or or_1 (IType, LIType, AIType, JIType);
  Comparator #(.width(3)) comparator_10 (.a(Inst[14:12]), .b(3'b101), .eq(comparator_10_eq));  // open: gt, lt
  Comparator #(.width(3)) comparator_11 (.a(Inst[14:12]), .b(3'b000), .eq(comparator_11_eq));  // open: gt, lt
  Comparator #(.width(3)) comparator_12 (.a(Inst[14:12]), .b(3'b001), .eq(comparator_12_eq));  // open: gt, lt
  Comparator #(.width(3)) comparator_13 (.a(Inst[14:12]), .b(3'b010), .eq(comparator_13_eq));  // open: gt, lt
  Comparator #(.width(3)) comparator_14 (.a(Inst[14:12]), .b(3'b011), .eq(comparator_14_eq));  // open: gt, lt
  Comparator #(.width(3)) comparator_15 (.a(Inst[14:12]), .b(3'b100), .eq(comparator_15_eq));  // open: gt, lt
  Comparator #(.width(3)) comparator_16 (.a(Inst[14:12]), .b(3'b101), .eq(comparator_16_eq));  // open: gt, lt
  Comparator #(.width(3)) comparator_17 (.a(Inst[14:12]), .b(3'b110), .eq(comparator_17_eq));  // open: gt, lt
  Comparator #(.width(3)) comparator_18 (.a(Inst[14:12]), .b(3'b111), .eq(comparator_18_eq));  // open: gt, lt
  or or_2 (or_2_out, comparator_10_eq, RType);
  not not_1 (not_1_out, IType);
  not not_2 (not_2_out, or_3_out);
  or or_3 (or_3_out, AIType, RType);
  Comparator #(.width(7)) comparator_19 (.a(multiplexer_1_out), .b({7{1'b0}}), .eq(comparator_19_eq));  // open: gt, lt
  // AND_Gate and_1 has open pins: in0=or_2_out, in1=not_1_out, out=open
  or or_4 (AluAdd, not_2_out, and_2_out);
  and and_2 (and_2_out, comparator_11_eq, comparator_19_eq);
  and and_3 (AluSll, comparator_12_eq, comparator_19_eq);
  and and_4 (AluSlt, comparator_13_eq, comparator_19_eq);
  and and_5 (AluSltu, comparator_14_eq, comparator_19_eq);
  and and_6 (AluXor, comparator_15_eq, comparator_19_eq);
  and and_7 (AluSrl, comparator_16_eq, comparator_19_eq);
  and and_8 (AluOr, comparator_17_eq, comparator_19_eq);
  and and_9 (AluAnd, comparator_18_eq, comparator_19_eq);
  Comparator #(.width(3)) comparator_20 (.a(Inst[14:12]), .b(3'b000), .eq(comparator_20_eq));  // open: gt, lt
  Comparator #(.width(3)) comparator_21 (.a(Inst[14:12]), .b(3'b100), .eq(comparator_21_eq));  // open: gt, lt
  Comparator #(.width(3)) comparator_22 (.a(Inst[14:12]), .b(3'b110), .eq(comparator_22_eq));  // open: gt, lt
  not not_3 (not_3_out, BrEq);
  Comparator #(.width(3)) comparator_23 (.a(Inst[14:12]), .b(3'b001), .eq(comparator_23_eq));  // open: gt, lt
  not not_4 (not_4_out, BrLT);
  Comparator #(.width(3)) comparator_24 (.a(Inst[14:12]), .b(3'b111), .eq(comparator_24_eq));  // open: gt, lt
  or or_5 (PCAluJ, JType, JIType);
  Multiplexer #(.width(7), .enable("false")) multiplexer_1 (
    .in0({7{1'b0}}), .in1(Inst[31:25]), .out(multiplexer_1_out), .sel(or_2_out));
  and and_10 (and_10_out, BrEq, comparator_20_eq);
  and and_11 (and_11_out, BrLT, comparator_21_eq);
  and and_12 (and_12_out, BrLT, comparator_22_eq);
  and and_13 (and_13_out, not_3_out, comparator_23_eq);
  and and_14 (and_14_out, not_4_out, comparator_24_eq);
  Comparator #(.width(7)) comparator_25 (.a(multiplexer_1_out), .b(7'b0000001), .eq(comparator_25_eq));  // open: gt, lt
  and and_15 (AluMult, comparator_11_eq, comparator_25_eq);
  and and_16 (AluMulh, comparator_12_eq, comparator_25_eq);
  // AND_Gate and_17 has open pins: in0=comparator_13_eq, in1=comparator_25_eq, out=open
  and and_18 (AluMulhu, comparator_14_eq, comparator_25_eq);
  // AND_Gate and_19 has open pins: in0=comparator_15_eq, in1=comparator_25_eq, out=open
  and and_20 (AluDivu, comparator_16_eq, comparator_25_eq);
  // AND_Gate and_21 has open pins: in0=comparator_17_eq, in1=comparator_25_eq, out=open
  and and_22 (AluRemu, comparator_18_eq, comparator_25_eq);
  or or_6 (or_6_out, and_10_out, and_11_out, and_12_out, and_13_out, and_14_out);
  Comparator #(.width(7)) comparator_26 (.a(multiplexer_1_out), .b(7'b0100000), .eq(comparator_26_eq));  // open: gt, lt
  or or_7 (InstSel, PCAluJ, PCAluB);
  and and_23 (AluSub, comparator_11_eq, comparator_26_eq);
  // AND_Gate and_24 has open pins: in0=comparator_12_eq, in1=comparator_26_eq, out=open
  // AND_Gate and_25 has open pins: in0=comparator_13_eq, in1=comparator_26_eq, out=open
  // AND_Gate and_26 has open pins: in0=comparator_14_eq, in1=comparator_26_eq, out=open
  // AND_Gate and_27 has open pins: in0=comparator_15_eq, in1=comparator_26_eq, out=open
  and and_28 (AluSra, comparator_16_eq, comparator_26_eq);
  // AND_Gate and_29 has open pins: in0=comparator_17_eq, in1=comparator_26_eq, out=open
  // AND_Gate and_30 has open pins: in0=comparator_18_eq, in1=comparator_26_eq, out=open
  and and_31 (PCAluB, BType, or_6_out);
  Multiplexer #(.width(4), .enable("false")) multiplexer_2 (
    .in0(4'b0000), .in1(4'b0001), .out(multiplexer_2_out), .sel(AluSub));
  Multiplexer #(.width(4), .enable("false")) multiplexer_3 (
    .in0(multiplexer_2_out), .in1(4'b0010), .out(multiplexer_3_out), .sel(AluMulh));
  Multiplexer #(.width(4), .enable("false")) multiplexer_4 (
    .in0(multiplexer_3_out), .in1(4'b0011), .out(multiplexer_4_out), .sel(AluMult));
  Multiplexer #(.width(4), .enable("false")) multiplexer_5 (
    .in0(multiplexer_4_out), .in1(4'b0100), .out(multiplexer_5_out), .sel(AluDivu));
  Multiplexer #(.width(4), .enable("false")) multiplexer_6 (
    .in0(multiplexer_5_out), .in1(4'b0101), .out(multiplexer_6_out), .sel(AluRemu));
  Comparator #(.width(3)) comparator_27 (.a(Inst[14:12]), .b(3'b110), .eq(comparator_27_eq));  // open: gt, lt
  Comparator #(.width(3)) comparator_28 (.a(Inst[14:12]), .b(3'b111), .eq(comparator_28_eq));  // open: gt, lt
  Multiplexer #(.width(3), .enable("false")) multiplexer_7 (
    .in0(3'b000), .in1(3'b000), .out(multiplexer_7_out), .sel(IType));
  or or_8 (or_8_out, BType, MemRW);
  or or_9 (or_9_out, comparator_27_eq, comparator_28_eq);
  Multiplexer #(.width(2), .enable("false")) multiplexer_8 (
    .in0(2'b00), .in1(2'b01), .out(multiplexer_8_out), .sel(or_10_out));
  or or_10 (or_10_out, BType, JType, AUType);
  not not_5 (BSel, RType);
  Multiplexer #(.width(4), .enable("false")) multiplexer_9 (
    .in0(multiplexer_6_out), .in1(4'b0110), .out(multiplexer_9_out), .sel(AluAnd));
  Multiplexer #(.width(4), .enable("false")) multiplexer_10 (
    .in0(multiplexer_9_out), .in1(4'b0111), .out(multiplexer_10_out), .sel(AluOr));
  Multiplexer #(.width(4), .enable("false")) multiplexer_11 (
    .in0(multiplexer_10_out), .in1(4'b1000), .out(multiplexer_11_out), .sel(AluXor));
  Multiplexer #(.width(4), .enable("false")) multiplexer_12 (
    .in0(multiplexer_11_out), .in1(4'b1001), .out(multiplexer_12_out), .sel(AluSll));
  Multiplexer #(.width(4), .enable("false")) multiplexer_13 (
    .in0(multiplexer_12_out), .in1(4'b1010), .out(multiplexer_13_out), .sel(AluSlt));
  Multiplexer #(.width(3), .enable("false")) multiplexer_14 (
    .in0(multiplexer_7_out), .in1(3'b001), .out(multiplexer_14_out), .sel(MemRW));
  not not_6 (RegWEn, or_8_out);
  and and_32 (BrUn, BType, or_9_out);
  Multiplexer #(.width(2), .enable("false")) multiplexer_15 (
    .in0(multiplexer_8_out), .in1(2'b10), .out(ASel), .sel(UType));
  Multiplexer #(.width(3), .enable("false")) multiplexer_16 (
    .in0(multiplexer_14_out), .in1(3'b010), .out(multiplexer_16_out), .sel(BType));
  or or_11 (or_11_out, AUType, UType);
  Multiplexer #(.width(4), .enable("false")) multiplexer_17 (
    .in0(multiplexer_13_out), .in1(4'b1011), .out(multiplexer_17_out), .sel(AluSra));
  Multiplexer #(.width(4), .enable("false")) multiplexer_18 (
    .in0(multiplexer_17_out), .in1(4'b1100), .out(multiplexer_18_out), .sel(AluSrl));
  Multiplexer #(.width(4), .enable("false")) multiplexer_19 (
    .in0(multiplexer_18_out), .in1(4'b1101), .out(multiplexer_19_out), .sel(AluMulhu));
  // Probe on ALUSel
  Multiplexer #(.width(3), .enable("false")) multiplexer_20 (
    .in0(multiplexer_16_out), .in1(3'b011), .out(multiplexer_20_out), .sel(or_11_out));
  Comparator #(.width(3)) comparator_29 (.a(Inst[14:12]), .b(3'b001), .eq(comparator_29_eq));  // open: gt, lt
  Comparator #(.width(3)) comparator_30 (.a(Inst[14:12]), .b(3'b101), .eq(comparator_30_eq));  // open: gt, lt
  Multiplexer #(.width(4), .enable("false")) multiplexer_21 (
    .in0(multiplexer_19_out), .in1(4'b1110), .out(multiplexer_21_out), .sel(AluSltu));
  Multiplexer #(.width(4), .enable("false")) multiplexer_22 (
    .in0(multiplexer_21_out), .in1(4'b0000), .out(ALUSel), .sel(AluAdd));
  Multiplexer #(.width(3), .enable("false")) multiplexer_23 (
    .in0(multiplexer_20_out), .in1(3'b100), .out(multiplexer_23_out), .sel(JType));
  or or_12 (or_12_out, comparator_29_eq, comparator_30_eq);
  Multiplexer #(.width(3), .enable("false")) multiplexer_24 (
    .in0(multiplexer_23_out), .in1(3'b101), .out(ImmSel), .sel(and_33_out));
  and and_33 (and_33_out, AIType, or_12_out);
  Comparator #(.width(3)) comparator_31 (.a(Inst[14:12]), .b(3'b000), .eq(comparator_31_eq));  // open: gt, lt
  Comparator #(.width(3)) comparator_32 (.a(Inst[14:12]), .b(3'b001), .eq(comparator_32_eq));  // open: gt, lt
  Comparator #(.width(3)) comparator_33 (.a(Inst[14:12]), .b(3'b010), .eq(comparator_33_eq));  // open: gt, lt
  Comparator #(.width(3)) comparator_34 (.a(Inst[14:12]), .b(3'b100), .eq(comparator_34_eq));  // open: gt, lt
  Comparator #(.width(3)) comparator_35 (.a(Inst[14:12]), .b(3'b101), .eq(comparator_35_eq));  // open: gt, lt
  Multiplexer #(.width(2), .enable("false")) multiplexer_25 (
    .in0(2'b01), .in1(2'b00), .out(multiplexer_25_out), .sel(LIType));
  Multiplexer #(.width(2), .enable("false")) multiplexer_26 (
    .in0(multiplexer_25_out), .in1(2'b10), .out(WBSel), .sel(or_13_out));
  or or_13 (or_13_out, JIType, JType);
  Multiplexer #(.width(3), .enable("false")) multiplexer_27 (
    .in0(3'b000), .in1(3'b000), .out(multiplexer_27_out), .sel(comparator_31_eq));
  Multiplexer #(.width(3), .enable("false")) multiplexer_28 (
    .in0(multiplexer_27_out), .in1(3'b001), .out(multiplexer_28_out), .sel(comparator_32_eq));
  // Probe on WBSel
  Multiplexer #(.width(3), .enable("false")) multiplexer_29 (
    .in0(multiplexer_28_out), .in1(3'b010), .out(multiplexer_29_out), .sel(comparator_33_eq));
  Multiplexer #(.width(3), .enable("false")) multiplexer_30 (
    .in0(multiplexer_29_out), .in1(3'b011), .out(multiplexer_30_out), .sel(comparator_34_eq));
  Multiplexer #(.width(3), .enable("false")) multiplexer_31 (
    .in0(multiplexer_30_out), .in1(3'b100), .out(DataSel), .sel(comparator_35_eq));
  // Probe on DataSel

  assign PCSel = InstSel;

  // Other names for the same wires on the sheet: Opcode[6:0] = Inst[6:0]; funct3[2:0] = Inst[14:12];
  //   funct7[6:0] = Inst[31:25]; SType = MemRW

  // Notes on the sheet:
  //   Load I-Type
  //   Arithmetic I-Type
  //   Jump I-Type
  //   jal
  //   jalr
  //   beq
  //   blt
  //   bltu
  //   bne
  //   bgeu
  //   PCSel
  //   Reg: 0, PC: 1, Zero:2
  //   I-type: 0; S-type: 1; B-type: 2; U-type: 3; J-type: 4
  //   RegWEn
  //   BrUn
  //   ASel
  //   BSel
  //   Reg: 0, Imm: 1
  //   ALUSel
  //   ImmSel
  //   lb: 0, lh: 1, lw:2, lbu:3, lhu:4
  //   Mem: 0, alu: 1, pc+4:2
  //   MemRW
  //   WBSel
  //   DataSel
endmodule

module test (
  input  [31:0] Add,
  input  WEn,
  input  clk,
  input  [31:0] WData,
  output [31:0] RData
);

  RAM #(.addrWidth(14), .dataWidth(32), .trigger("falling"), .databus("bibus")) ram_1 (
    .addr(Add[13:0]), .we(WEn), .oe(1'b1), .clk(clk), .din(WData), .dout(RData));
endmodule
