// Logisim project mem.circ as structural Verilog: 1 circuit, main circuit main
module main (
  input  [31:0] Address,
  input  MemRW,
  input  clk,
  input  [31:0] DataW,
  output [31:0] DataR
);

  RAM #(.addrWidth(24), .dataWidth(32), .trigger("falling"), .databus("bibus")) DMEM (
    .addr(Address[23:0]), .we(MemRW), .oe(1'b1), .clk(clk), .din(DataW), .dout(DataR));
endmodule
